# Fritzing sketch mini Project 1 (saved by Fritzing 0.9.3b)
breadboards: 1

parts:
  U1 = NodeMCU V1.0
  R1 = Resistor [tolerance=±5% resistance=220 package=THT]
  LED1 = LED - 5mm [color="Green (555nm)" package="5 mm [THT]"]
  LED2 = LED - 5mm [color="Yellow (585nm)" package="5 mm [THT]"]
  LED3 = LED - 5mm [color="Red (633nm)" package="5 mm [THT]"]

nets:
  N1: U1.D0, LED3.anode
  N2: U1.D1, LED2.anode
  N3: U1.D2, LED1.anode
  N4: U1.GND, R1.Pin_0
  N5: R1.Pin_1, LED1.cathode, LED2.cathode, LED3.cathode

custom parts:
  NodeMCU V1.0: ESP8266 based NodeMCU
